# Fritzing sketch genéticos (saved by Fritzing 1.0.4)
breadboards: 1

parts:
  Mod1 = Raspberry Pi Pico
  Componente1 = OLED Monochrome 128x32 I2C [part_number=931]
  DAC1 = MCP4725 12-bit DAC Breakout
  R1 = Rotary Potentiometer (Small) [maximum_resistance=10kΩ knob_status=50% power=0.5W package=THT]
  R2 = Resistor [tolerance=±5% resistance=1k power=0.25W package="0805 [SMD]"]
  S5 = Pushbutton [package="[THT]"]

nets:
  GND: Mod1.pin_3, Mod1.pin_8, Mod1.pin_13, Mod1.pin_18, Mod1.pin_23, Mod1.pin_28, Mod1.pin_33, Mod1.pin_38, Mod1.pin_42, Componente1.GND, DAC1.GND, R1.leg1, R2.Pin_0
  N1: Mod1.pin_4, R2.Pin_1, S5.Pin_3, S5.Pin_4
  N2: Mod1.pin_9, Componente1.SDA, DAC1.SDA
  N3: Mod1.pin_10, Componente1.SCL, DAC1.SCL
  N4: Mod1.pin_30, DAC1.VOUT
  N5: Mod1.pin_31, R1.wiper
  3.3V: Mod1.pin_36, Componente1.3.3V, DAC1.VDD, R1.leg2, S5.Pin_1, S5.Pin_2

custom parts:
  Raspberry Pi Pico: Raspberry Pi Pico. Based around the RP2040 microcontroller the Pico is a low cost microcontroller device bringing Raspberry Pi quality, cost, and easy of use to the microcontroller space. Jan 2021, Split part in to two versions: tht (this one) and SMD. This one will drill holes for a .1 in header in pcb to allow plugging in the module as well as providing pads to solder the module to the top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
  OLED Monochrome 128x32 I2C: These displays are small, only about 1" diagonal, but very readable due to the high contrast of an OLED display. This display is made of 128x32 individual white OLED pixels, each one is turned on or off by the controller chip. Because the display makes its own light, no backlight is required. This reduces the power required to run the OLED and is why the display has such high contrast; we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
  MCP4725 12-bit DAC Breakout: MCP4725 12-bit Digital-to-Analog Converter
